# Fritzing sketch BinkyTreeCircuit (saved by Fritzing 0.9.1b)

parts:
  NEOPIXEL1 = Neopixel Strip -- Black (60/m)
  Part1 = Arduino Yun
  R1 = Resistor [tolerance=±5% resistance=1M package=THT]
  U1 = TOUCH [package=touch2]

nets:
  +5V: NEOPIXEL1.+5V, Part1.5V
  N1: NEOPIXEL1.DI, Part1.D12/MISO
  GND: NEOPIXEL1.GND, Part1.GND
  N2: Part1.D10_PWM/SS, R1.Pin_0
  N3: Part1.D7, R1.Pin_1, U1.T2

notes:
  NeoPixel String
  Bell (capacitive sensor)
  1-Megohm resistor

custom parts:
  Neopixel Strip -- Black (60/m): Neopixel Strip, Black, 60 pixels per meter.
